// Logisim project AT3.circ as structural Verilog: 1 circuit, main circuit main
module main (
  input  A,
  input  B,
  input  C,
  input  D
);

  wire not_1_out, not_2_out, not_3_out, not_4_out, not_5_out, not_6_out, not_7_out, not_8_out, not_9_out,
       S1_out, S2_out, S3_out, S4_out, S_out;

  not not_1 (not_1_out, A);
  not not_2 (not_2_out, B);
  not not_3 (not_3_out, C);
  not not_4 (not_4_out, A);
  not not_5 (not_5_out, B);
  not not_6 (not_6_out, A);
  not not_7 (not_7_out, B);
  not not_8 (not_8_out, C);
  not not_9 (not_9_out, D);
  and S1 (S1_out, not_1_out, not_2_out, not_3_out, D);
  and S2 (S2_out, not_4_out, not_5_out, C, D);
  and S3 (S3_out, not_6_out, not_7_out, not_8_out, not_9_out);
  and S4 (S4_out, A, B, C, D);
  or S (S_out, S1_out, S2_out, S3_out, S4_out);
  LED led_1 (.in(S_out));

  // Notes on the sheet:
  //   S1 = !A!B!CD
  //   S2 = !A!BCD
  //   S3 = A!B!C!D
  //   S4 = ABCD
endmodule
