// Logisim project at 2.circ as structural Verilog: 1 circuit, main circuit main
module main (
  input  A,
  input  B,
  input  D,
  input  E,
  input  F,
  input  C
);

  wire and_1_out, and_2_out, or_1_out, or_2_out, or_3_out, S3_out;

  buf or_1 (or_1_out, A);  // OR_Gate
  or or_2 (or_2_out, B, D);
  and and_1 (and_1_out, or_1_out, or_2_out);
  and and_2 (and_2_out, E, F);
  buf S3 (S3_out, C);  // OR_Gate
  or or_3 (or_3_out, and_1_out, and_2_out, S3_out);
  LED led_1 (.in(or_3_out));

  // Notes on the sheet:
  //   S1-1
  //   S1-2
  //   S1
  //   S2
  //   S
endmodule
